# Fritzing sketch remote-control (saved by Fritzing 0.8.3b)
breadboards: 2

parts:
  U1 = atmega168 [package=dip]
  Y1 = Crystal [frequency="20 MHz" package=THT]
  C1 = Ceramic Capacitor [capacitance=22pF package="100 mil [THT, multilayer]"]
  C2 = Ceramic Capacitor [capacitance=22pF package="100 mil [THT, multilayer]"]
  S1 = Pushbutton [package="[THT]"]
  S2 = Pushbutton [package="[THT]"]
  S3 = Pushbutton [package="[THT]"]
  S4 = Pushbutton [package="[THT]"]
  S5 = Pushbutton [package="[THT]"]
  S6 = Pushbutton [package="[THT]"]
  S7 = Pushbutton [package="[THT]"]
  S8 = Pushbutton [package="[THT]"]
  S9 = Pushbutton [package="[THT]"]
  S10 = Pushbutton [package="[THT]"]
  S11 = Pushbutton [package="[THT]"]
  S12 = Pushbutton [package="[THT]"]
  S13 = Pushbutton [package="[THT]"]
  S14 = Pushbutton [package="[THT]"]
  S15 = Pushbutton [package="[THT]"]
  VCC1 = Battery block 9V
  U2 = mystery part, 3 pins [chip_label=?]
  Q1 = PNP-Transistor [package="TO92 [THT]"]
  R1 = Resistor [tolerance=±5% resistance=33k package=THT]
  C3 = Electrolytic Capacitor [capacitance=1µF package="100 mil [THT, electrolytic]"]
  C4 = Electrolytic Capacitor [capacitance=1µF package="100 mil [THT, electrolytic]"]
  Q2 = NPN-Transistor [package="TO92 [THT]"]
  R2 = Resistor [tolerance=±5% resistance=27k package=THT]
  C5 = Ceramic Capacitor [capacitance=100nF package="100 mil [THT, multilayer]"]
  R3 = Resistor [tolerance=±5% resistance=220 package=THT]

nets:
  N1: U1.RESET, C5.1, R3.Pin_0
  N2: U1.VCC, U1.AVCC, R3.Pin_1
  N3: U1.GND, VCC1.-, U2.pin2, C3.-, C4.-, Q2.E
  N4: U1.XLAT2, Y1.pin_1, C2.1
  N5: Y1.pin_0, C1.0
  N6: C1.1, C2.0
  N7: S1.Pin_1, S1.Pin_2
  N8: S1.Pin_3, S1.Pin_4
  N9: S2.Pin_1, S2.Pin_2
  N10: S2.Pin_3, S2.Pin_4
  N11: S3.Pin_1, S3.Pin_2
  N12: S3.Pin_3, S3.Pin_4
  N13: S4.Pin_1, S4.Pin_2
  N14: S4.Pin_3, S4.Pin_4
  N15: S5.Pin_1, S5.Pin_2
  N16: S5.Pin_3, S5.Pin_4
  N17: S6.Pin_1, S6.Pin_2
  N18: S6.Pin_3, S6.Pin_4
  N19: S7.Pin_1, S7.Pin_2
  N20: S7.Pin_3, S7.Pin_4
  N21: S8.Pin_1, S8.Pin_2
  N22: S8.Pin_3, S8.Pin_4
  N23: S9.Pin_1, S9.Pin_2
  N24: S9.Pin_3, S9.Pin_4
  N25: S10.Pin_1, S10.Pin_2
  N26: S10.Pin_3, S10.Pin_4
  N27: S11.Pin_1, S11.Pin_2
  N28: S11.Pin_3, S11.Pin_4
  N29: S12.Pin_1, S12.Pin_2
  N30: S12.Pin_3, S12.Pin_4
  N31: S13.Pin_1, S13.Pin_2
  N32: S13.Pin_3, S13.Pin_4
  N33: S14.Pin_1, S14.Pin_2
  N34: S14.Pin_3, S14.Pin_4
  N35: S15.Pin_1, S15.Pin_2
  N36: S15.Pin_3, S15.Pin_4
  N37: VCC1.+, Q1.E, R1.Pin_0
  N38: U2.pin1, Q1.C, C3.+
  N39: U2.pin3, C4.+
  N40: Q1.B, R1.Pin_1, R2.Pin_1
  N41: Q2.C, R2.Pin_0
